# Fritzing sketch circuit_example (saved by Fritzing 0.9.0b)
circuit board: 9.7861cm x 5.82075cm
breadboards: 1

parts:
  Parte1 = Arduino Uno (Rev3)
  U1 = 74HC595 [package="DIP16 [THT]"]
  U2 = 74HC595 [package="DIP16 [THT]"]
  R1 = Resistor [tolerance=±5% resistance=220 package=THT]
  R2 = Resistor [tolerance=±5% resistance=220 package=THT]
  R3 = Resistor [tolerance=±5% resistance=220 package=THT]
  R4 = Resistor [tolerance=±5% resistance=220 package=THT]
  R5 = Resistor [tolerance=±5% resistance=220 package=THT]
  R6 = Resistor [tolerance=±5% resistance=220 package=THT]
  R7 = Resistor [tolerance=±5% resistance=220 package=THT]
  R8 = Resistor [tolerance=±5% resistance=220 package=THT]
  R9 = Resistor [tolerance=±5% resistance=220 package=THT]
  R10 = Resistor [tolerance=±5% resistance=220 package=THT]
  R11 = Resistor [tolerance=±5% resistance=220 package=THT]
  R13 = Resistor [tolerance=±5% resistance=220 package=THT]
  R14 = Resistor [tolerance=±5% resistance=220 package=THT]
  R15 = Resistor [tolerance=±5% resistance=220 package=THT]
  R16 = Resistor [tolerance=±5% resistance=220 package=THT]
  LED1 = LED - 5mm [color="Red (633nm)" package="5 mm [THT]"]
  LED2 = LED - 5mm [color="Red (633nm)" package="5 mm [THT]"]
  LED3 = LED - 5mm [color="Red (633nm)" package="5 mm [THT]"]
  LED4 = LED - 5mm [color="Red (633nm)" package="5 mm [THT]"]
  LED5 = LED - 5mm [color="Red (633nm)" package="5 mm [THT]"]
  LED6 = LED - 5mm [color="Red (633nm)" package="5 mm [THT]"]
  LED7 = LED - 5mm [color="Red (633nm)" package="5 mm [THT]"]
  LED8 = LED - 5mm [color="Red (633nm)" package="5 mm [THT]"]
  LED9 = LED - 5mm [color="Red (633nm)" package="5 mm [THT]"]
  LED10 = LED - 5mm [color="Red (633nm)" package="5 mm [THT]"]
  LED11 = LED - 5mm [color="Red (633nm)" package="5 mm [THT]"]
  LED12 = LED - 5mm [color="Red (633nm)" package="5 mm [THT]"]
  LED13 = LED - 5mm [color="Red (633nm)" package="5 mm [THT]"]
  LED14 = LED - 5mm [color="Red (633nm)" package="5 mm [THT]"]
  LED15 = LED - 5mm [color="Red (633nm)" package="5 mm [THT]"]
  LED16 = LED - 5mm [color="Red (633nm)" package="5 mm [THT]"]
  R12 = Resistor [tolerance=±5% resistance=220 package=THT]
  Pad1 = Pad [width=1.1499185982802 height=3.46746705119806 connect=center]  # not connected

nets:
  N1: Parte1.D8, U1.ST_CP, U2.ST_CP
  N2: Parte1.D11_PWM/MOSI, U1.DS
  N3: Parte1.D12/MISO, U1.SH_CP, U2.SH_CP
  GND: Parte1.GND, U1.GND, U1.OE, U2.GND, U2.OE, R1.Pin_0, R2.Pin_0, R3.Pin_0, R4.Pin_0, R5.Pin_0, R6.Pin_0, R7.Pin_0, R8.Pin_0, R9.Pin_1, R10.Pin_1, R11.Pin_1, R13.Pin_1, R14.Pin_1, R15.Pin_1, R16.Pin_1, R12.Pin_1
  VCC: Parte1.5V, U1.MR, U1.VCC, U2.MR, U2.VCC
  N4: U1.Q1, LED7.anode
  N5: U1.Q2, LED6.anode
  N6: U1.Q3, LED5.anode
  N7: U1.Q4, LED4.anode
  N8: U1.Q5, LED3.anode
  N9: U1.Q6, LED2.anode
  N10: U1.Q7, LED1.anode
  N11: U1.Q7', U2.DS
  N12: U1.Q0, LED8.anode
  N13: U2.Q1, LED12.anode
  N14: U2.Q2, LED14.anode
  N15: U2.Q3, LED16.anode
  N16: U2.Q4, LED9.anode
  N17: U2.Q5, LED11.anode
  N18: U2.Q6, LED13.anode
  N19: U2.Q7, LED15.anode
  N20: U2.Q0, LED10.anode
  N21: R1.Pin_1, LED1.cathode
  N22: R2.Pin_1, LED2.cathode
  N23: R3.Pin_1, LED3.cathode
  N24: R4.Pin_1, LED4.cathode
  N25: R5.Pin_1, LED5.cathode
  N26: R6.Pin_1, LED6.cathode
  N27: R7.Pin_1, LED7.cathode
  N28: R8.Pin_1, LED8.cathode
  N29: R9.Pin_0, LED15.cathode
  N30: R10.Pin_0, LED13.cathode
  N31: R11.Pin_0, LED11.cathode
  N32: R13.Pin_0, LED16.cathode
  N33: R14.Pin_0, LED14.cathode
  N34: R15.Pin_0, LED12.cathode
  N35: R16.Pin_0, LED10.cathode
  N36: LED9.cathode, R12.Pin_0

notes:
  IC 1
  IC 2
